# Fritzing sketch Fritz_Model (saved by Fritzing 0.7.12b)
breadboards: 1

parts:
  Arduino1 = Arduino
  R1 = Resistor [tolerance=±5% resistance=220 package=THT]
  R2 = Resistor [tolerance=±5% resistance=220 package=THT]
  R3 = Resistor [tolerance=±5% resistance=220 package=THT]
  R4 = Resistor [tolerance=±5% resistance=220 package=THT]
  R5 = Resistor [tolerance=±5% resistance=220 package=THT]
  R6 = Resistor [tolerance=±5% resistance=220 package=THT]
  R7 = Resistor [tolerance=±5% resistance=220 package=THT]
  R8 = Resistor [tolerance=±5% resistance=220 package=THT]
  LED1 = LED - 5mm [color="Red (633nm)" package="5 mm [THT]"]
  LED2 = LED - 5mm [color="Red (633nm)" package="5 mm [THT]"]
  LED3 = LED - 5mm [color="Red (633nm)" package="5 mm [THT]"]
  LED4 = LED - 5mm [color="Red (633nm)" package="5 mm [THT]"]
  LED5 = LED - 5mm [color="Red (633nm)" package="5 mm [THT]"]
  LED6 = LED - 5mm [color="Red (633nm)" package="5 mm [THT]"]
  LED7 = LED - 5mm [color="Red (633nm)" package="5 mm [THT]"]
  LED8 = LED - 5mm [color="Red (633nm)" package="5 mm [THT]"]

nets:
  N1: Arduino1.D9, LED8.anode
  N2: Arduino1.D8, LED7.anode
  N3: Arduino1.D7, LED6.anode
  N4: Arduino1.D6, LED5.anode
  N5: Arduino1.D5, LED4.anode
  N6: Arduino1.D4, LED3.anode
  N7: Arduino1.D3, LED2.anode
  N8: Arduino1.D2, LED1.anode
  N9: Arduino1.GND, R1.Pin_0, R2.Pin_0, R3.Pin_0, R4.Pin_0, R5.Pin_0, R6.Pin_0, R7.Pin_0, R8.Pin_0
  N10: R1.Pin_1, LED1.cathode
  N11: R2.Pin_1, LED3.cathode
  N12: R3.Pin_1, LED2.cathode
  N13: R4.Pin_1, LED4.cathode
  N14: R5.Pin_1, LED5.cathode
  N15: R6.Pin_1, LED6.cathode
  N16: R7.Pin_1, LED7.cathode
  N17: R8.Pin_1, LED8.cathode
